# Fritzing sketch circuit (saved by Fritzing 0.9.3b)

parts:
  Part2 = Arduino Nano 33 IOT
  Part3 = Arduino Nano Every
  R1 = Resistor [tolerance=±5% resistance=1k package="0805 [SMD]"]
  R2 = Resistor [tolerance=±5% resistance=1k package="0805 [SMD]"]
  R3 = Resistor [tolerance=±5% resistance=2.2k package="0805 [SMD]"]

nets:
  N1: Part2.RX, R1.Pin_0, R3.Pin_1
  N2: Part2.TX, R2.Pin_0
  GND: Part2.GND, Part2.D13~, Part3.GND, Part3.D13~
  N3: Part3.RX, R1.Pin_1
  N4: Part3.TX, R2.Pin_1

notes:
  iot 33
  every
  RX
  TX
  GND
  10V/2A DC p/s
  +V
  0.4-4.5 pressure transducer
  +5V
  sense
  A0
  1k
  2k2

custom parts:
  Arduino Nano 33 IOT: The Arduino Nano 33 IoT is the easiest and cheapest point of entry to enhance existing devices (and creating new ones) to be part of the IoT and designing pico-network applications. Whether you are looking at building a sensor network connected to your office or home router, or if you want to create a BLE device sending data to a cellphone, the Nano 33 IoT is your one-stop-solution for many of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
  Arduino Nano Every: The Nano Every is Arduino’s 5V compatible board in the smallest available form factor: 45x18mm! The Arduino Nano is the preferred board for many projects requiring a small and easy to use microcontroller board. The small footprint and low price, make the Nano Every particularly suited for wearable inventions, low cost robotics, electronic musical instruments, and general use to control smaller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
